// Logisim project ALU.circ as structural Verilog: 1 circuit, main circuit main
module main (
  input  [31:0] X,
  input  [31:0] Y,
  input  Reloj,
  input  LOAD,
  input  Reset,
  input  [1:0] in_6
);

  wire demultiplexer_1_out0, demultiplexer_1_out1;

  Demultiplexer #(.select(2)) demultiplexer_1 (
    .out0(demultiplexer_1_out0), .out1(demultiplexer_1_out1), .in(LOAD), .sel(in_6));  // open: out2, out3
  Register #(.width(32)) register_1 (.D(X), .en(demultiplexer_1_out0), .clk(Reloj), .clr(Reset));  // open: Q
  Register #(.width(32)) register_2 (.D(Y), .en(demultiplexer_1_out1), .clk(Reloj), .clr(Reset));  // open: Q
endmodule
