// Logisim project Computadora.circ as structural Verilog: 12 circuits, main circuit ALU
module Computadora (
  input  IN_CMD
);

  wire clock_1_out, clock_2_out, control_unit_1_load_signal, control_unit_1_reset_pc,
       control_unit_1_reset_signal_out, demultiplexer_1_out0, demultiplexer_1_out1, loader_1_load_alu,
       loader_1_load_general_register, loader_1_load_if_while, loader_1_load_in_ram, loader_1_load_mdr,
       loader_1_load_ram_register, loader_1_load_vram_gpu, multiplexer_3_out, not_1_out, RESET_out;
  wire [1:0] control_unit_1_pc_gpu_op, control_unit_1_pc_op, loader_1_alu_register_n,
       loader_1_if_while_register_n;
  wire [2:0] loader_1_general_register_op;
  wire [3:0] control_unit_1_router_op, router_1_out_alu_opcode;
  wire [4:0] control_unit_1_load_op, control_unit_1_router_op_2;
  wire [7:0] multiplexer_1_out;
  wire [10:0] demultiplexer_2_out1;
  wire [14:0] multiplexer_4_out, rgb_video_1_p6;
  wire [15:0] control_unit_1_pc_gpu_jump, gpu_step_1_data_out;
  wire [23:0] control_unit_1_out_step, control_unit_1_pc_jump, if_while_1_dir_out,
       program_counter_1_data_out, ram_1_dout, router_1_data_gpu_vram, router_1_if_while_code,
       router_1_if_while_end;
  wire [31:0] alu_1_out_alu, control_unit_1_router_data, register_1_q, registros_generales_1_out_r0,
       registros_generales_1_out_r1, registros_generales_1_out_r2, registros_generales_1_out_r3,
       registros_generales_1_out_r4, registros_generales_1_out_r5, registros_generales_1_out_r6,
       registros_generales_1_out_r7, registros_ram_1_out_r0, registros_ram_1_out_r1, registros_ram_1_out_r2,
       registros_ram_1_out_r3, registros_ram_1_out_r4, registros_ram_1_out_r5, registros_ram_1_out_r6,
       registros_ram_1_out_r7, router_1_if_while_condicion, router_1_out_alu_x, router_1_out_alu_y,
       router_1_out_mdr, router_1_out_r0_general, router_1_out_r1_general, router_1_out_r2_general,
       router_1_out_r3_general, router_1_out_r4_general, router_1_out_r5_general, router_1_out_r6_general,
       router_1_out_r7_general, STACK_dout;
  wire [31:4] router_1_out_alu_opcode_2;
  wire [31:24] router_1_data_gpu_vram_2, router_1_if_while_code_2, router_1_if_while_end_2;
  wire [36:0] INSTRUCTION_data;
  wire [63:0] Bit_Map_Caracteres_data;

  Clock clock_1 (.out(clock_1_out));
  Button RESET (.out(RESET_out));
  LOADER loader_1 (
    .LOAD_SIGNAL(control_unit_1_load_signal), .LOAD_OP(control_unit_1_load_op),
    .LOAD_RAM_REGISTER(loader_1_load_ram_register), .GENERAL_REGISTER_OP(loader_1_general_register_op),
    .LOAD_GENERAL_REGISTER(loader_1_load_general_register), .ALU_REGISTER_N(loader_1_alu_register_n),
    .LOAD_ALU(loader_1_load_alu), .LOAD_MDR(loader_1_load_mdr), .LOAD_IN_RAM(loader_1_load_in_ram),
    .IF_While_Register_N(loader_1_if_while_register_n), .LOAD_IF_WHILE(loader_1_load_if_while),
    .LOAD_VRAM_GPU(loader_1_load_vram_gpu));
  ALU alu_1 (
    .X(router_1_out_alu_x), .Y(router_1_out_alu_y), .Reloj(clock_1_out), .LOAD(loader_1_load_alu),
    .Reset(control_unit_1_reset_signal_out), .LOAD_REGISTER_NUMBER(loader_1_alu_register_n),
    .OPERACION(router_1_out_alu_opcode), .OUT_ALU(alu_1_out_alu));
  Program_Counter program_counter_1 (
    .Reloj(clock_1_out), .DATA_JUMP(control_unit_1_pc_jump), .RESET(control_unit_1_reset_pc),
    .PC_OP(control_unit_1_pc_op), .DATA_OUT(program_counter_1_data_out));
  IF_WHILE if_while_1 (
    .DATA_CONDICION(router_1_if_while_condicion[0]), .DIR_CODE(router_1_if_while_code),
    .DIR_END(router_1_if_while_end), .LOAD(loader_1_load_if_while), .LOAD_OP(loader_1_if_while_register_n),
    .Reloj(clock_1_out), .RESET(control_unit_1_reset_signal_out), .Dir_OUT(if_while_1_dir_out));
  ROUTER router_1 (
    .IN_R0_RAM(registros_ram_1_out_r0), .IN_R1_RAM(registros_ram_1_out_r1),
    .IN_R2_RAM(registros_ram_1_out_r2), .IN_R3_RAM(registros_ram_1_out_r3),
    .IN_R4_RAM(registros_ram_1_out_r4), .IN_R5_RAM(registros_ram_1_out_r5),
    .IN_R6_RAM(registros_ram_1_out_r6), .IN_R7_RAM(registros_ram_1_out_r7),
    .IN_R0_General(registros_generales_1_out_r0), .IN_R1_General(registros_generales_1_out_r1),
    .IN_R2_General(registros_generales_1_out_r2), .IN_R3_General(registros_generales_1_out_r3),
    .IN_R4_General(registros_generales_1_out_r4), .IN_R5_General(registros_generales_1_out_r5),
    .IN_R6_General(registros_generales_1_out_r6), .IN_R7_General(registros_generales_1_out_r7),
    .ALU_RESULT(alu_1_out_alu), .IN_CU(control_unit_1_router_data), .ORIGIN(control_unit_1_router_op_2),
    .DESTINY(control_unit_1_router_op), .OUT_R0_General(router_1_out_r0_general),
    .OUT_R1_General(router_1_out_r1_general), .OUT_R2_General(router_1_out_r2_general),
    .OUT_R3_General(router_1_out_r3_general), .OUT_R4_General(router_1_out_r4_general),
    .OUT_R5_General(router_1_out_r5_general), .OUT_R6_General(router_1_out_r6_general),
    .OUT_R7_General(router_1_out_r7_general), .OUT_MDR(router_1_out_mdr), .OUT_ALU_X(router_1_out_alu_x),
    .OUT_ALU_Y(router_1_out_alu_y), .OUT_ALU_OPCODE({router_1_out_alu_opcode_2, router_1_out_alu_opcode}),
    .IF_WHILE_CONDICION(router_1_if_while_condicion),
    .IF_WHILE_CODE({router_1_if_while_code_2, router_1_if_while_code}),
    .IF_WHILE_END({router_1_if_while_end_2, router_1_if_while_end}),
    .DATA_GPU_VRAM({router_1_data_gpu_vram_2, router_1_data_gpu_vram}));
  Control_Unit control_unit_1 (
    .PC_GPU_JUMP(control_unit_1_pc_gpu_jump), .Reset_Signal(RESET_out), .STEP_TO_JUMP(if_while_1_dir_out),
    .Reloj(clock_1_out), .Instruction(INSTRUCTION_data), .PC_GPU_OP(control_unit_1_pc_gpu_op),
    .Reset_Signal_Out(control_unit_1_reset_signal_out), .OUT_STEP(control_unit_1_out_step),
    .LOAD_SIGNAL(control_unit_1_load_signal), .LOAD_OP(control_unit_1_load_op),
    .ROUTER_OP({control_unit_1_router_op_2, control_unit_1_router_op}), .PC_JUMP(control_unit_1_pc_jump),
    .PC_OP(control_unit_1_pc_op), .RESET_PC(control_unit_1_reset_pc), .ROUTER_DATA(control_unit_1_router_data));
  ROM #(.addrWidth(24), .dataWidth(37)) INSTRUCTION (.addr(control_unit_1_out_step), .data(INSTRUCTION_data));
  Register #(.width(32)) register_1 (
    .D(router_1_out_mdr), .en(loader_1_load_mdr), .clk(clock_1_out), .Q(register_1_q),
    .clr(control_unit_1_reset_signal_out));
  REGISTROS_RAM registros_ram_1 (
    .DATA_IN(STACK_dout), .RESET(control_unit_1_reset_signal_out), .Reloj(clock_1_out),
    .LOAD(loader_1_load_ram_register), .OUT_R0(registros_ram_1_out_r0), .OUT_R1(registros_ram_1_out_r1),
    .OUT_R2(registros_ram_1_out_r2), .OUT_R3(registros_ram_1_out_r3), .OUT_R4(registros_ram_1_out_r4),
    .OUT_R5(registros_ram_1_out_r5), .OUT_R6(registros_ram_1_out_r6), .OUT_R7(registros_ram_1_out_r7));
  RAM #(.addrWidth(24), .dataWidth(32)) STACK (
    .addr(program_counter_1_data_out), .we(loader_1_load_in_ram), .oe(loader_1_load_ram_register),
    .clk(clock_1_out), .din(register_1_q), .dout(STACK_dout));
  Registros_Generales registros_generales_1 (
    .RESET(control_unit_1_reset_signal_out), .Reloj(clock_1_out),
    .LOAD_REGISTER_N(loader_1_general_register_op), .LOAD(loader_1_load_general_register),
    .OUT_R0(registros_generales_1_out_r0), .OUT_R1(registros_generales_1_out_r1),
    .OUT_R2(registros_generales_1_out_r2), .OUT_R3(registros_generales_1_out_r3),
    .OUT_R4(registros_generales_1_out_r4), .OUT_R5(registros_generales_1_out_r5),
    .OUT_R6(registros_generales_1_out_r6), .OUT_R7(registros_generales_1_out_r7),
    .IN_R0(router_1_out_r0_general), .IN_R1(router_1_out_r1_general), .IN_R2(router_1_out_r2_general),
    .IN_R3(router_1_out_r3_general), .IN_R4(router_1_out_r4_general), .IN_R5(router_1_out_r5_general),
    .IN_R6(router_1_out_r6_general), .IN_R7(router_1_out_r7_general));
  Clock clock_2 (.out(clock_2_out));
  GPU_STEP gpu_step_1 (
    .DATA_JUMP(control_unit_1_pc_gpu_jump), .Reloj(clock_2_out), .RESET(control_unit_1_reset_signal_out),
    .STEP_OP(control_unit_1_pc_gpu_op), .DATA_OUT(gpu_step_1_data_out));
  Demultiplexer demultiplexer_1 (
    .out0(demultiplexer_1_out0), .out1(demultiplexer_1_out1), .in(1'b1), .sel(loader_1_load_vram_gpu));
  // RGB_Video #(.height(256), .width(256)) rgb_video_1: pin names not known; wires that end beside it: control_unit_1_reset_signal_out, clock_2_out, 1'b1, gpu_step_1_data_out[7:0], gpu_step_1_data_out[15:8], rgb_video_1_p6
  Demultiplexer #(.width(11)) demultiplexer_2 (
    .out1(demultiplexer_2_out1), .in({1'b0, gpu_step_1_data_out[15:11], gpu_step_1_data_out[7:3]}),
    .sel(not_1_out));  // open: out0
  RAM #(.addrWidth(11), .dataWidth(24)) ram_1 (
    .addr(demultiplexer_2_out1), .we(demultiplexer_1_out1), .oe(demultiplexer_1_out0), .clk(clock_2_out),
    .din(router_1_data_gpu_vram), .dout(ram_1_dout));
  ROM #(.addrWidth(24), .dataWidth(64)) Bit_Map_Caracteres (.addr(ram_1_dout), .data(Bit_Map_Caracteres_data));
  not not_1 (not_1_out, IN_CMD);
  Multiplexer #(.select(3), .width(8)) multiplexer_1 (
    .in0(Bit_Map_Caracteres_data[7:0]), .in1(Bit_Map_Caracteres_data[15:8]),
    .in2(Bit_Map_Caracteres_data[23:16]), .in3(Bit_Map_Caracteres_data[31:24]),
    .in4(Bit_Map_Caracteres_data[39:32]), .in5(Bit_Map_Caracteres_data[47:40]),
    .in6(Bit_Map_Caracteres_data[55:48]), .in7(Bit_Map_Caracteres_data[63:56]), .out(multiplexer_1_out),
    .sel(gpu_step_1_data_out[10:8]));
  Multiplexer #(.width(15)) multiplexer_2 (
    .in1(multiplexer_4_out), .out(rgb_video_1_p6), .sel(not_1_out));  // open: in0
  Multiplexer #(.select(3)) multiplexer_3 (
    .in0(multiplexer_1_out[0]), .in1(multiplexer_1_out[1]), .in2(multiplexer_1_out[2]),
    .in3(multiplexer_1_out[3]), .in4(multiplexer_1_out[4]), .in5(multiplexer_1_out[5]),
    .in6(multiplexer_1_out[6]), .in7(multiplexer_1_out[7]), .out(multiplexer_3_out),
    .sel(gpu_step_1_data_out[2:0]));
  Multiplexer #(.width(15)) multiplexer_4 (
    .in0({15{1'b0}}), .in1({15{1'b1}}), .out(multiplexer_4_out), .sel(multiplexer_3_out));

  // Notes on the sheet:
  //   contents of INSTRUCTION (hex, n*v repeats v):
  //   13*0 1000000000
  //   contents of Bit_Map_Caracteres (hex, n*v repeats v):
  //   41417f4141413e00 3f41413f41413f00 3e41010101413e00 1f21414141211f00 7f01017f01017f00 101017f01017f00
  //   3c42417901423c00 4141417f41414100 7f08080808087f00 1c22202020202000 4141211f21414100
  //   7e02020202020200 4141414149556300 4161514945434100 6151494543007f00 3e41414141413e00 1013f4141413f00
  //   5e21414141413e00 41413f4141413f00 3e41403e01413e00 808080808087f00 3e41414141414100 814142222414100
  //   142a2a4141414100 4141221c22414100 3e41407e41414100 7f01021c20407f00 1e213e20201e0000
  //   1e22221e02020200 1e210101211e0000 3c22223c20202000 1e21013f211e0000 1010f0101221c00 3844407844447800
  //   1111110f01010100 808080800080000 1c22202020002000 909070909010000 c02020202020200 494949493f000000
  //   242424241c000000 242424241c003c00 1e2121211e000000 404043c44443c00 2020202063a0000 3e403c027c000000
  //   182404041f040400 3c22222222000000 814222200000000 142a2a2200000000 2424182424000000 1c203c2222220000
  //   3e021c203e000000 3e0808080a0c0800 7e020c3040423c00 1e20201e20201e00 2020203e22242400
  //   3c42403c02027e00 18241c0424241800 404080810203e00 3c42423c42423c00 1824203824241800 3c42464a72423c00
  //   808087f08080800 7f00000000 492a1c7f1c2a4900 202040408080000 400000000000000 204000000000000
  //   400000000040000 204000000040000 4000404040404000 202020202000200 4000408080a0400 2050101020002000
  //   a0a0a00 2020200 143e143e14000000 81e281c0a3c0800 7e00007e000000 2010080408102000 408102010080400
  //   4020202020204000 204040404040200 6020202020206000 604040404040600 2152240812254200 40a0400
  //   7f00000000000000 324c000000 1c023a3a221c0000 6010101810106000 304040c04040300 110a0400
  //   4040202010100000 5c22521c22221c00 808080808080800
endmodule

// CU
module Control_Unit (
  input  Reset_Signal,
  input  [23:0] STEP_TO_JUMP,
  input  Reloj,
  input  [36:0] Instruction,
  output [15:0] PC_GPU_JUMP,
  output LOAD_SIGNAL,
  output Reset_Signal_Out,
  output [4:0] LOAD_OP,
  output [8:0] ROUTER_OP,
  output [23:0] PC_JUMP,
  output [23:0] OUT_STEP,
  output [1:0] PC_OP,
  output RESET_PC,
  output [31:0] ROUTER_DATA,
  output [1:0] PC_GPU_OP
);

  wire and_1_out, and_2_out, comparator_1_eq, comparator_2_eq, demultiplexer_1_out0, demultiplexer_1_out1,
       demultiplexer_1_out2, demultiplexer_1_out3, demultiplexer_1_out4, demultiplexer_1_out5,
       demultiplexer_1_out6, demultiplexer_1_out7, demultiplexer_1_out8, not_1_out, not_2_out, not_3_out,
       register_1_q, register_2_q;
  wire [31:0] demultiplexer_2_out0, demultiplexer_2_out1, demultiplexer_2_out2, demultiplexer_2_out3,
       demultiplexer_2_out4, demultiplexer_2_out5, demultiplexer_2_out6, demultiplexer_2_out7,
       demultiplexer_2_out8;

  Register #(.width(1)) register_1 (.D(not_3_out), .en(1'b1), .clk(Reloj), .Q(register_1_q), .clr(Reset_Signal_Out));
  Comparator #(.mode("unsigned"), .width(1)) comparator_1 (
    .a(Instruction[36]), .b(1'b1), .eq(comparator_1_eq));  // open: gt, lt
  and and_1 (and_1_out, Instruction[32], Instruction[33], Instruction[34], not_2_out);
  Boton_Signal boton_signal_1 (.Signal_In(Reset_Signal), .Reloj(Reloj), .Signal_Out(Reset_Signal_Out));
  not not_1 (not_1_out, comparator_1_eq);
  not not_2 (not_2_out, Instruction[35]);
  Comparator #(.mode("unsigned"), .width(1)) comparator_2 (
    .a(register_1_q), .b(1'b1), .eq(comparator_2_eq));  // open: gt, lt
  not not_3 (not_3_out, register_1_q);
  Register #(.width(1)) register_2 (.D(and_1_out), .en(1'b1), .clk(Reloj), .Q(register_2_q), .clr(Reset_Signal_Out));
  and and_2 (and_2_out, comparator_2_eq, not_1_out);
  CU_STEP cu_step_1 (
    .DATA_JUMP(STEP_TO_JUMP), .ADVANCE(and_2_out), .Reloj(Reloj), .RESET(Reset_Signal_Out),
    .STEP_OP(register_2_q), .DATA_OUT(OUT_STEP));
  Demultiplexer #(.select(4)) demultiplexer_1 (
    .out0(demultiplexer_1_out0), .out1(demultiplexer_1_out1), .out2(demultiplexer_1_out2),
    .out3(demultiplexer_1_out3), .out4(demultiplexer_1_out4), .out5(demultiplexer_1_out5),
    .out6(demultiplexer_1_out6), .out7(demultiplexer_1_out7), .out8(demultiplexer_1_out8), .in(1'b1),
    .sel(Instruction[35:32]));  // open: out9, out10, out11, out12, out13, out14, out15
  Demultiplexer #(.select(4), .width(32)) demultiplexer_2 (
    .out0(demultiplexer_2_out0), .out1(demultiplexer_2_out1), .out2(demultiplexer_2_out2),
    .out3(demultiplexer_2_out3), .out4(demultiplexer_2_out4), .out5(demultiplexer_2_out5),
    .out6(demultiplexer_2_out6), .out7(demultiplexer_2_out7), .out8(demultiplexer_2_out8),
    .in(Instruction[31:0]), .sel(Instruction[35:32]));  // open: out9, out10, out11, out12, out13, out14, out15
  Register #(.width(1)) register_3 (
    .D(demultiplexer_2_out0[0]), .en(demultiplexer_1_out0), .clk(Reloj), .Q(LOAD_SIGNAL),
    .clr(Reset_Signal_Out));
  Register #(.width(5)) register_4 (
    .D(demultiplexer_2_out1[4:0]), .en(demultiplexer_1_out1), .clk(Reloj), .Q(LOAD_OP), .clr(Reset_Signal_Out));
  Register #(.width(9)) register_5 (
    .D(demultiplexer_2_out2[8:0]), .en(demultiplexer_1_out2), .clk(Reloj), .Q(ROUTER_OP),
    .clr(Reset_Signal_Out));
  Register #(.width(24)) register_6 (
    .D(demultiplexer_2_out3[23:0]), .en(demultiplexer_1_out3), .clk(Reloj), .Q(PC_JUMP),
    .clr(Reset_Signal_Out));
  Register #(.width(2)) register_7 (
    .D(demultiplexer_2_out4[1:0]), .en(demultiplexer_1_out4), .clk(Reloj), .Q(PC_OP), .clr(Reset_Signal_Out));
  Register #(.width(1)) register_8 (
    .D(demultiplexer_2_out5[0]), .en(demultiplexer_1_out5), .clk(Reloj), .Q(RESET_PC), .clr(Reset_Signal_Out));
  Register #(.width(32)) register_9 (
    .D(demultiplexer_2_out6), .en(demultiplexer_1_out6), .clk(Reloj), .Q(ROUTER_DATA), .clr(Reset_Signal_Out));
  Register #(.width(16)) register_10 (
    .D(demultiplexer_2_out7[15:0]), .en(demultiplexer_1_out7), .clk(Reloj), .Q(PC_GPU_JUMP),
    .clr(Reset_Signal_Out));
  Register #(.width(2)) register_11 (
    .D(demultiplexer_2_out8[1:0]), .en(demultiplexer_1_out8), .clk(Reloj), .Q(PC_GPU_OP),
    .clr(Reset_Signal_Out));
endmodule

module ALU (
  input  [31:0] X,
  input  [31:0] Y,
  input  Reloj,
  input  LOAD,
  input  Reset,
  input  [3:0] OPERACION,
  input  [1:0] LOAD_REGISTER_NUMBER,
  output [31:0] OUT_ALU
);

  wire comparator_1_eq, comparator_1_gt, comparator_1_lt, demultiplexer_1_out0, demultiplexer_1_out1,
       demultiplexer_1_out2, demultiplexer_1_out3;
  wire [3:0] register_3_q;
  wire [31:0] adder_1_out, and_1_out, bit_extender_1_out, bit_extender_2_out, bit_extender_3_out,
       divider_1_out, multiplexer_1_out, multiplier_1_out, nand_1_out, nor_1_out, or_1_out, register_1_q,
       register_2_q, subtractor_1_out, xnor_1_out, xor_1_out;

  Demultiplexer #(.select(2)) demultiplexer_1 (
    .out0(demultiplexer_1_out0), .out1(demultiplexer_1_out1), .out2(demultiplexer_1_out2),
    .out3(demultiplexer_1_out3), .in(LOAD), .sel(LOAD_REGISTER_NUMBER));
  Register #(.width(32)) register_1 (.D(X), .en(demultiplexer_1_out0), .clk(Reloj), .Q(register_1_q), .clr(Reset));
  Register #(.width(32)) register_2 (.D(Y), .en(demultiplexer_1_out1), .clk(Reloj), .Q(register_2_q), .clr(Reset));
  Adder #(.width(32)) adder_1 (.a(register_1_q), .b(register_2_q), .out(adder_1_out));  // open: cin, cout
  Subtractor #(.width(32)) subtractor_1 (
    .a(register_1_q), .b(register_2_q), .out(subtractor_1_out));  // open: bin, bout
  Multiplier #(.width(32)) multiplier_1 (
    .a(register_1_q), .b(register_2_q), .out(multiplier_1_out));  // open: cin, cout
  Divider #(.width(32)) divider_1 (.a(register_1_q), .b(register_2_q), .out(divider_1_out));  // open: upper, rem
  Comparator #(.mode("unsigned"), .width(32)) comparator_1 (
    .a(register_1_q), .b(register_2_q), .gt(comparator_1_gt), .eq(comparator_1_eq), .lt(comparator_1_lt));
  assign and_1_out = register_1_q & register_2_q;  // AND_Gate and_1, 32 bits wide
  assign nand_1_out = ~(register_1_q & register_2_q);  // NAND_Gate nand_1, 32 bits wide
  assign or_1_out = register_1_q | register_2_q;  // OR_Gate or_1, 32 bits wide
  assign nor_1_out = ~(register_1_q | register_2_q);  // NOR_Gate nor_1, 32 bits wide
  assign xor_1_out = register_1_q ^ register_2_q;  // XOR_Gate xor_1, 32 bits wide
  assign xnor_1_out = ~(register_1_q ^ register_2_q);  // XNOR_Gate xnor_1, 32 bits wide
  assign bit_extender_1_out = {{31{1'b0}}, comparator_1_gt};  // Bit_Extender bit_extender_1
  assign bit_extender_2_out = {{31{1'b0}}, comparator_1_eq};  // Bit_Extender bit_extender_2
  assign bit_extender_3_out = {{31{1'b0}}, comparator_1_lt};  // Bit_Extender bit_extender_3
  Multiplexer #(.select(4), .width(32)) multiplexer_1 (
    .in0(adder_1_out), .in1(subtractor_1_out), .in2(multiplier_1_out), .in3(divider_1_out), .in4(and_1_out),
    .in5(nand_1_out), .in6(or_1_out), .in7(nor_1_out), .in8(xor_1_out), .in9(xnor_1_out),
    .in10(bit_extender_1_out), .in11(bit_extender_2_out), .in12(bit_extender_3_out), .out(multiplexer_1_out),
    .sel(register_3_q));  // open: in13, in14, in15
  Register #(.width(4)) register_3 (
    .D(OPERACION), .en(demultiplexer_1_out2), .clk(Reloj), .Q(register_3_q), .clr(Reset));
  Register #(.width(32)) register_4 (
    .D(multiplexer_1_out), .en(demultiplexer_1_out3), .clk(Reloj), .Q(OUT_ALU), .clr(Reset));
endmodule

// GEN_REGIS
module Registros_Generales (
  input  RESET,
  input  Reloj,
  input  [31:0] IN_R0,
  input  [31:0] IN_R1,
  input  [31:0] IN_R2,
  input  [31:0] IN_R3,
  input  [31:0] IN_R4,
  input  [31:0] IN_R5,
  input  [31:0] IN_R6,
  input  [31:0] IN_R7,
  input  [2:0] LOAD_REGISTER_N,
  input  LOAD,
  output [31:0] OUT_R0,
  output [31:0] OUT_R1,
  output [31:0] OUT_R2,
  output [31:0] OUT_R3,
  output [31:0] OUT_R4,
  output [31:0] OUT_R5,
  output [31:0] OUT_R6,
  output [31:0] OUT_R7
);

  wire demultiplexer_1_out0, demultiplexer_1_out1, demultiplexer_1_out2, demultiplexer_1_out3,
       demultiplexer_1_out4, demultiplexer_1_out5, demultiplexer_1_out6, demultiplexer_1_out7;

  Register #(.width(32)) R0 (.D(IN_R0), .en(demultiplexer_1_out0), .clk(Reloj), .Q(OUT_R0), .clr(RESET));
  Register #(.width(32)) R1 (.D(IN_R1), .en(demultiplexer_1_out1), .clk(Reloj), .Q(OUT_R1), .clr(RESET));
  Register #(.width(32)) R2 (.D(IN_R2), .en(demultiplexer_1_out2), .clk(Reloj), .Q(OUT_R2), .clr(RESET));
  Demultiplexer #(.select(3)) demultiplexer_1 (
    .out0(demultiplexer_1_out0), .out1(demultiplexer_1_out1), .out2(demultiplexer_1_out2),
    .out3(demultiplexer_1_out3), .out4(demultiplexer_1_out4), .out5(demultiplexer_1_out5),
    .out6(demultiplexer_1_out6), .out7(demultiplexer_1_out7), .in(LOAD), .sel(LOAD_REGISTER_N));
  Register #(.width(32)) R3 (.D(IN_R3), .en(demultiplexer_1_out3), .clk(Reloj), .Q(OUT_R3), .clr(RESET));
  Register #(.width(32)) R4 (.D(IN_R4), .en(demultiplexer_1_out4), .clk(Reloj), .Q(OUT_R4), .clr(RESET));
  Register #(.width(32)) R5 (.D(IN_R5), .en(demultiplexer_1_out5), .clk(Reloj), .Q(OUT_R5), .clr(RESET));
  Register #(.width(32)) R6 (.D(IN_R6), .en(demultiplexer_1_out6), .clk(Reloj), .Q(OUT_R6), .clr(RESET));
  Register #(.width(32)) R7 (.D(IN_R7), .en(demultiplexer_1_out7), .clk(Reloj), .Q(OUT_R7), .clr(RESET));
endmodule

// RAM_REGIS
module REGISTROS_RAM (
  input  [31:0] DATA_IN,
  input  RESET,
  input  Reloj,
  input  LOAD,
  output [31:0] OUT_R0,
  output [31:0] OUT_R1,
  output [31:0] OUT_R2,
  output [31:0] OUT_R3,
  output [31:0] OUT_R4,
  output [31:0] OUT_R5,
  output [31:0] OUT_R6,
  output [31:0] OUT_R7
);

  Register #(.width(32)) R0 (.D(DATA_IN), .en(LOAD), .clk(Reloj), .Q(OUT_R0), .clr(RESET));
  Register #(.width(32)) R1 (.D(OUT_R0), .en(LOAD), .clk(Reloj), .Q(OUT_R1), .clr(RESET));
  Register #(.width(32)) R2 (.D(OUT_R1), .en(LOAD), .clk(Reloj), .Q(OUT_R2), .clr(RESET));
  Register #(.width(32)) R3 (.D(OUT_R2), .en(LOAD), .clk(Reloj), .Q(OUT_R3), .clr(RESET));
  Register #(.width(32)) R4 (.D(OUT_R3), .en(LOAD), .clk(Reloj), .Q(OUT_R4), .clr(RESET));
  Register #(.width(32)) R5 (.D(OUT_R4), .en(LOAD), .clk(Reloj), .Q(OUT_R5), .clr(RESET));
  Register #(.width(32)) R6 (.D(OUT_R5), .en(LOAD), .clk(Reloj), .Q(OUT_R6), .clr(RESET));
  Register #(.width(32)) R7 (.D(OUT_R6), .en(LOAD), .clk(Reloj), .Q(OUT_R7), .clr(RESET));
endmodule

module ROUTER (
  input  [31:0] IN_R0_RAM,
  input  [31:0] IN_R1_RAM,
  input  [31:0] IN_R2_RAM,
  input  [31:0] IN_R3_RAM,
  input  [31:0] IN_R4_RAM,
  input  [31:0] IN_R5_RAM,
  input  [31:0] IN_R6_RAM,
  input  [31:0] IN_R7_RAM,
  input  [31:0] IN_R0_General,
  input  [31:0] IN_R1_General,
  input  [31:0] IN_R2_General,
  input  [31:0] IN_R3_General,
  input  [31:0] IN_R4_General,
  input  [31:0] IN_R5_General,
  input  [31:0] IN_R6_General,
  input  [31:0] IN_R7_General,
  input  [31:0] ALU_RESULT,
  input  [3:0] DESTINY,
  input  [4:0] ORIGIN,
  input  [31:0] IN_CU,
  output [31:0] OUT_R0_General,
  output [31:0] OUT_R1_General,
  output [31:0] OUT_R2_General,
  output [31:0] OUT_R3_General,
  output [31:0] OUT_R4_General,
  output [31:0] OUT_R5_General,
  output [31:0] OUT_R6_General,
  output [31:0] OUT_R7_General,
  output [31:0] OUT_MDR,
  output [31:0] OUT_ALU_X,
  output [31:0] OUT_ALU_Y,
  output [31:0] OUT_ALU_OPCODE,
  output [31:0] IF_WHILE_CONDICION,
  output [31:0] IF_WHILE_CODE,
  output [31:0] IF_WHILE_END,
  output [31:0] DATA_GPU_VRAM
);

  wire [31:0] multiplexer_1_out;

  Multiplexer #(.select(5), .width(32)) multiplexer_1 (
    .in0(IN_R0_RAM), .in1(IN_R1_RAM), .in2(IN_R2_RAM), .in3(IN_R3_RAM), .in4(IN_R4_RAM), .in5(IN_R5_RAM),
    .in6(IN_R6_RAM), .in7(IN_R7_RAM), .in8(IN_R0_General), .in9(IN_R1_General), .in10(IN_R2_General),
    .in11(IN_R3_General), .in12(IN_R4_General), .in13(IN_R5_General), .in14(IN_R6_General),
    .in15(IN_R7_General), .in16(ALU_RESULT), .in17(IN_CU), .out(multiplexer_1_out), .sel(ORIGIN));  // open: in18, in19, in20, in21, in22, in23, in24, in25, in26, in27, in28, in29, in30, in31
  Demultiplexer #(.select(4), .width(32)) demultiplexer_1 (
    .out0(OUT_R0_General), .out1(OUT_R1_General), .out2(OUT_R2_General), .out3(OUT_R3_General),
    .out4(OUT_R4_General), .out5(OUT_R5_General), .out6(OUT_R6_General), .out7(OUT_R7_General),
    .out8(OUT_MDR), .out9(OUT_ALU_X), .out10(OUT_ALU_Y), .out11(OUT_ALU_OPCODE), .out12(IF_WHILE_CONDICION),
    .out13(IF_WHILE_CODE), .out14(IF_WHILE_END), .out15(DATA_GPU_VRAM), .in(multiplexer_1_out), .sel(DESTINY));
endmodule

module LOADER (
  input  LOAD_SIGNAL,
  input  [4:0] LOAD_OP,
  output LOAD_RAM_REGISTER,
  output [2:0] GENERAL_REGISTER_OP,
  output LOAD_GENERAL_REGISTER,
  output [1:0] ALU_REGISTER_N,
  output LOAD_ALU,
  output LOAD_MDR,
  output LOAD_IN_RAM,
  output [1:0] IF_While_Register_N,
  output LOAD_IF_WHILE,
  output LOAD_VRAM_GPU
);

  wire demultiplexer_1_out1, demultiplexer_1_out2, demultiplexer_1_out3, demultiplexer_1_out4,
       demultiplexer_1_out5, demultiplexer_1_out6, demultiplexer_1_out7, demultiplexer_1_out8,
       demultiplexer_1_out9, demultiplexer_1_out10, demultiplexer_1_out11, demultiplexer_1_out12,
       demultiplexer_1_out15, demultiplexer_1_out16, demultiplexer_1_out17, demultiplexer_1_out18;

  Demultiplexer #(.select(5)) demultiplexer_1 (
    .out0(LOAD_RAM_REGISTER), .out1(demultiplexer_1_out1), .out2(demultiplexer_1_out2),
    .out3(demultiplexer_1_out3), .out4(demultiplexer_1_out4), .out5(demultiplexer_1_out5),
    .out6(demultiplexer_1_out6), .out7(demultiplexer_1_out7), .out8(demultiplexer_1_out8),
    .out9(demultiplexer_1_out9), .out10(demultiplexer_1_out10), .out11(demultiplexer_1_out11),
    .out12(demultiplexer_1_out12), .out13(LOAD_MDR), .out14(LOAD_IN_RAM), .out15(demultiplexer_1_out15),
    .out16(demultiplexer_1_out16), .out17(demultiplexer_1_out17), .out18(demultiplexer_1_out18),
    .out19(LOAD_VRAM_GPU), .in(LOAD_SIGNAL), .sel(LOAD_OP));  // open: out20, out21, out22, out23, out24, out25, out26, out27, out28, out29, out30, out31
  Priority_Encoder priority_encoder_1 (
    .in0(demultiplexer_1_out1), .in1(demultiplexer_1_out2), .in2(demultiplexer_1_out3),
    .in3(demultiplexer_1_out4), .in4(demultiplexer_1_out5), .in5(demultiplexer_1_out6),
    .in6(demultiplexer_1_out7), .in7(demultiplexer_1_out8), .out(GENERAL_REGISTER_OP),
    .gs(LOAD_GENERAL_REGISTER));  // open: en_in, en_out
  Priority_Encoder #(.select(2)) priority_encoder_2 (
    .in0(demultiplexer_1_out9), .in1(demultiplexer_1_out10), .in2(demultiplexer_1_out11),
    .in3(demultiplexer_1_out12), .out(ALU_REGISTER_N), .gs(LOAD_ALU));  // open: en_out, en_in
  Priority_Encoder #(.select(2)) priority_encoder_3 (
    .in0(demultiplexer_1_out15), .in1(demultiplexer_1_out16), .in2(demultiplexer_1_out17),
    .in3(demultiplexer_1_out18), .out(IF_While_Register_N), .gs(LOAD_IF_WHILE));  // open: en_out, en_in
endmodule

// PC
module Program_Counter (
  input  Reloj,
  input  [23:0] DATA_JUMP,
  input  RESET,
  input  [1:0] PC_OP,
  output [23:0] DATA_OUT
);

  wire demultiplexer_1_out1, demultiplexer_1_out2;
  wire [23:0] adder_1_out, bit_extender_1_out, multiplexer_1_out;

  Register #(.width(24)) register_1 (.D(multiplexer_1_out), .en(1'b1), .clk(Reloj), .Q(DATA_OUT), .clr(RESET));
  assign bit_extender_1_out = {{23{1'b0}}, demultiplexer_1_out1};  // Bit_Extender bit_extender_1
  Demultiplexer #(.select(2)) demultiplexer_1 (
    .out1(demultiplexer_1_out1), .out2(demultiplexer_1_out2), .in(1'b1), .sel(PC_OP));  // open: out0, out3
  Adder #(.width(24)) adder_1 (.a(DATA_OUT), .b(bit_extender_1_out), .out(adder_1_out));  // open: cin, cout
  Multiplexer #(.width(24)) multiplexer_1 (
    .in0(adder_1_out), .in1(DATA_JUMP), .out(multiplexer_1_out), .sel(demultiplexer_1_out2));
endmodule

// BTN
module Boton_Signal (
  input  Signal_In,
  input  Reloj,
  output Signal_Out
);

  wire d_ff_1_q, not_1_out;

  D_Flip_Flop d_ff_1 (.D(Signal_In), .clk(Reloj), .Q(d_ff_1_q));  // open: Qn, preset, reset
  not not_1 (not_1_out, d_ff_1_q);
  and and_1 (Signal_Out, Signal_In, not_1_out);
endmodule

// IF_WH
module IF_WHILE (
  input  DATA_CONDICION,
  input  [23:0] DIR_CODE,
  input  LOAD,
  input  [1:0] LOAD_OP,
  input  Reloj,
  input  RESET,
  input  [23:0] DIR_END,
  output [23:0] Dir_OUT
);

  wire comparator_1_eq, demultiplexer_1_out0, demultiplexer_1_out1, demultiplexer_1_out2,
       demultiplexer_1_out3, register_1_q;
  wire [23:0] multiplexer_1_out, register_2_q, register_3_q;

  Register #(.width(1)) register_1 (
    .D(DATA_CONDICION), .en(demultiplexer_1_out0), .clk(Reloj), .Q(register_1_q), .clr(RESET));
  Demultiplexer #(.select(2)) demultiplexer_1 (
    .out0(demultiplexer_1_out0), .out1(demultiplexer_1_out1), .out2(demultiplexer_1_out2),
    .out3(demultiplexer_1_out3), .in(LOAD), .sel(LOAD_OP));
  Comparator #(.width(1)) comparator_1 (.a(register_1_q), .b(1'b1), .eq(comparator_1_eq));  // open: gt, lt
  Register #(.width(24)) register_2 (
    .D(DIR_CODE), .en(demultiplexer_1_out1), .clk(Reloj), .Q(register_2_q), .clr(RESET));
  Register #(.width(24)) register_3 (
    .D(DIR_END), .en(demultiplexer_1_out2), .clk(Reloj), .Q(register_3_q), .clr(RESET));
  Multiplexer #(.width(24)) multiplexer_1 (
    .in0(register_2_q), .in1(register_3_q), .out(multiplexer_1_out), .sel(comparator_1_eq));
  Register #(.width(24)) register_4 (
    .D(multiplexer_1_out), .en(demultiplexer_1_out3), .clk(Reloj), .Q(Dir_OUT), .clr(RESET));
endmodule

// STEP
module CU_STEP (
  input  Reloj,
  input  [23:0] DATA_JUMP,
  input  RESET,
  input  STEP_OP,
  input  ADVANCE,
  output [23:0] DATA_OUT
);

  wire demultiplexer_1_out0, demultiplexer_1_out1;
  wire [23:0] adder_1_out, bit_extender_1_out, multiplexer_1_out;

  Register #(.width(24)) register_1 (.D(multiplexer_1_out), .en(1'b1), .clk(Reloj), .Q(DATA_OUT), .clr(RESET));
  assign bit_extender_1_out = {{23{1'b0}}, demultiplexer_1_out0};  // Bit_Extender bit_extender_1
  Demultiplexer demultiplexer_1 (.out0(demultiplexer_1_out0), .out1(demultiplexer_1_out1), .in(ADVANCE), .sel(STEP_OP));
  Adder #(.width(24)) adder_1 (.a(DATA_OUT), .b(bit_extender_1_out), .out(adder_1_out));  // open: cin, cout
  Multiplexer #(.width(24)) multiplexer_1 (
    .in0(adder_1_out), .in1(DATA_JUMP), .out(multiplexer_1_out), .sel(demultiplexer_1_out1));
endmodule

// PC
module GPU_STEP (
  input  Reloj,
  input  [15:0] DATA_JUMP,
  input  RESET,
  input  [1:0] STEP_OP,
  output [15:0] DATA_OUT
);

  wire demultiplexer_1_out0, demultiplexer_1_out1;
  wire [15:0] adder_1_out, bit_extender_1_out, multiplexer_1_out;

  Register #(.width(16)) register_1 (.D(multiplexer_1_out), .en(1'b1), .clk(Reloj), .Q(DATA_OUT), .clr(RESET));
  assign bit_extender_1_out = {{15{1'b0}}, demultiplexer_1_out0};  // Bit_Extender bit_extender_1
  Demultiplexer #(.select(2)) demultiplexer_1 (
    .out0(demultiplexer_1_out0), .out1(demultiplexer_1_out1), .in(1'b1), .sel(STEP_OP));  // open: out2, out3
  Adder #(.width(16)) adder_1 (.a(DATA_OUT), .b(bit_extender_1_out), .out(adder_1_out));  // open: cin, cout
  Multiplexer #(.width(16)) multiplexer_1 (
    .in0(adder_1_out), .in1(DATA_JUMP), .out(multiplexer_1_out), .sel(demultiplexer_1_out1));
endmodule
