// Logisim project MicroControlador.circ as structural Verilog: 24 circuits, main circuit main
module main (
  output [19:0] out_1,
  output [7:0] R0,
  output [7:0] R1,
  output [7:0] R2,
  output [7:0] R3,
  output [7:0] R4,
  output [7:0] R5,
  output [7:0] R6,
  output [7:0] R7,
  output [7:0] Program_Counter,
  output [4:0] LOAD_OP,
  output [1:0] PC_Instruction,
  output [15:0] STEP
);

  wire clock_1_out, cu_1_advance, cu_1_load_signal, cu_1_reset_pc, cu_1_reset_signal_2,
       loader_manager_1_load_alu, loader_manager_1_load_general_register, loader_manager_1_load_in_ram,
       loader_manager_1_load_ir, loader_manager_1_load_mdr, loader_manager_1_load_ram_register, not_1_out,
       RESET_out;
  wire [1:0] loader_manager_1_alu_register_n, loader_manager_1_ir_op;
  wire [2:0] loader_manager_1_general_register_op;
  wire [3:0] cu_1_alu_operacion, cu_1_destiny, router_manager_1_out_ir_opcode;
  wire [4:0] cu_1_origin;
  wire [7:0] alu_1_result, controlled_buffer_1_out, cu_1_pc_jump, MDR_output, ram_1_data,
       registros_generales_1_o_r0, registros_generales_1_o_r1, registros_generales_1_o_r2,
       registros_generales_1_o_r3, registros_generales_1_o_r4, registros_generales_1_o_r5,
       registros_generales_1_o_r6, registros_generales_1_o_r7, router_manager_1_out_alu_x,
       router_manager_1_out_alu_y, router_manager_1_out_ir_r0, router_manager_1_out_ir_r0_2,
       router_manager_1_out_mdr, router_manager_1_out_r0_general, router_manager_1_out_r1_general,
       router_manager_1_out_r2_general, router_manager_1_out_r3_general, router_manager_1_out_r4_general,
       router_manager_1_out_r5_general, router_manager_1_out_r6_general, router_manager_1_out_r7_general;
  wire [12:0] rom_1_data;

  Clock clock_1 (.out(clock_1_out));
  Button RESET (.out(RESET_out));
  Loader_Manager loader_manager_1 (
    .LOAD_SIGNAL(cu_1_load_signal), .LOAD_OP(LOAD_OP),
    .LOAD_RAM_Register(loader_manager_1_load_ram_register),
    .General_Register_OP(loader_manager_1_general_register_op),
    .LOAD_General_Register(loader_manager_1_load_general_register),
    .ALU_Register_N(loader_manager_1_alu_register_n), .LOAD_ALU(loader_manager_1_load_alu),
    .LOAD_MDR(loader_manager_1_load_mdr), .LOAD_IN_RAM(loader_manager_1_load_in_ram),
    .IR_OP(loader_manager_1_ir_op), .LOAD_IR(loader_manager_1_load_ir));
  ALU alu_1 (
    .X(router_manager_1_out_alu_x), .Y(router_manager_1_out_alu_y), .LOAD(loader_manager_1_load_alu),
    .LOAD_R_N(loader_manager_1_alu_register_n), .Reloj(clock_1_out), .RESET(cu_1_reset_signal_2),
    .Operacion(cu_1_alu_operacion), .Result(alu_1_result));
  Instruction_Register instruction_register_1 (
    .Dato_In_R0(router_manager_1_out_ir_r0), .Dato_OPCODE(router_manager_1_out_ir_opcode),
    .Load(loader_manager_1_load_ir), .Dato_In_R1(router_manager_1_out_ir_r0_2), .Reset(cu_1_reset_signal_2),
    .LOAD_R_N(loader_manager_1_ir_op), .Reloj(clock_1_out), .Output(out_1));
  PC pc_1 (
    .Dato_Salto(cu_1_pc_jump), .PC_INSTRUCTION(PC_Instruction), .Reloj(cu_1_advance), .RESET(cu_1_reset_pc),
    .Dato_Salida(Program_Counter));
  CU cu_1 (
    .RESET_SIGNAL(RESET_out), .Reloj(clock_1_out), .IR_INPUT(out_1), .PC_COUNTER_INPUT(Program_Counter),
    .ROM_STEP(STEP), .Instruction(rom_1_data), .ADVANCE(cu_1_advance), .RESET_SIGNAL_2(cu_1_reset_signal_2),
    .LOAD_SIGNAL(cu_1_load_signal), .LOAD_OP(LOAD_OP), .ORIGIN(cu_1_origin), .DESTINY(cu_1_destiny),
    .ALU_OPERACION(cu_1_alu_operacion), .PC_JUMP(cu_1_pc_jump), .PC_OP(PC_Instruction),
    .RESET_PC(cu_1_reset_pc));
  Router_Manager router_manager_1 (
    .In_R0_RAM(R0), .In_R1_RAM(R1), .In_R2_RAM(R2), .In_R3_RAM(R3), .In_R4_RAM(R4), .In_R5_RAM(R5),
    .In_R6_RAM(R6), .In_R7_RAM(R7), .In_R0_General(registros_generales_1_o_r0),
    .In_R1_General(registros_generales_1_o_r1), .In_R2_General(registros_generales_1_o_r2),
    .In_R3_General(registros_generales_1_o_r3), .In_R4_General(registros_generales_1_o_r4),
    .In_R5_General(registros_generales_1_o_r5), .In_R6_General(registros_generales_1_o_r6),
    .In_R7_General(registros_generales_1_o_r7), .IN_ALU_R(alu_1_result),
    .OUT_IR_R0(router_manager_1_out_ir_r0), .OUT_IR_R0_2(router_manager_1_out_ir_r0_2), .ORIGIN(cu_1_origin),
    .DESTINY(cu_1_destiny), .OUT_R0_General(router_manager_1_out_r0_general),
    .OUT_R1_General(router_manager_1_out_r1_general), .OUT_R2_General(router_manager_1_out_r2_general),
    .OUT_R3_General(router_manager_1_out_r3_general), .OUT_R4_General(router_manager_1_out_r4_general),
    .OUT_R5_General(router_manager_1_out_r5_general), .OUT_R6_General(router_manager_1_out_r6_general),
    .OUT_R7_General(router_manager_1_out_r7_general), .OUT_MDR(router_manager_1_out_mdr),
    .OUT_ALU_X(router_manager_1_out_alu_x), .OUT_ALU_Y(router_manager_1_out_alu_y),
    .OUT_IR_OPCODE(router_manager_1_out_ir_opcode));
  Registros_RAM registros_ram_1 (
    .Input(controlled_buffer_1_out), .O_R0(R0), .O_R1(R1), .O_R2(R2), .O_R3(R3), .O_R4(R4), .O_R5(R5),
    .O_R6(R6), .O_R7(R7), .LOAD(loader_manager_1_load_ram_register), .Reset(cu_1_reset_signal_2),
    .Reloj(cu_1_advance));
  ROM #(.addrWidth(16), .dataWidth(13)) rom_1 (.addr(STEP), .data(rom_1_data));  // open: sel
  Registros_Generales registros_generales_1 (
    .RESET(cu_1_reset_signal_2), .Reloj(clock_1_out), .O_R0(registros_generales_1_o_r0),
    .O_R1(registros_generales_1_o_r1), .O_R2(registros_generales_1_o_r2), .O_R3(registros_generales_1_o_r3),
    .O_R4(registros_generales_1_o_r4), .O_R5(registros_generales_1_o_r5), .O_R6(registros_generales_1_o_r6),
    .O_R7(registros_generales_1_o_r7), .In_R0(router_manager_1_out_r0_general),
    .In_R1(router_manager_1_out_r1_general), .In_R2(router_manager_1_out_r2_general),
    .LOAD(loader_manager_1_load_general_register), .In_R3(router_manager_1_out_r3_general),
    .In_R4(router_manager_1_out_r4_general), .In_R5(router_manager_1_out_r5_general),
    .In_R6(router_manager_1_out_r6_general), .LOAD_R_N(loader_manager_1_general_register_op),
    .In_R7(router_manager_1_out_r7_general));
  not not_1 (not_1_out, loader_manager_1_load_in_ram);
  assign controlled_buffer_1_out = not_1_out ? ram_1_data : 8'bz;  // Controlled_Buffer controlled_buffer_1
  RAM ram_1 (
    .addr(Program_Counter), .data(ram_1_data), .clk(clock_1_out), .ld(not_1_out), .clr(cu_1_reset_signal_2));  // open: sel
  assign ram_1_data = loader_manager_1_load_in_ram ? MDR_output : 8'bz;  // Controlled_Buffer controlled_buffer_2
  Registro_8_bits MDR (
    .Load(loader_manager_1_load_mdr), .Data_In(router_manager_1_out_mdr), .Reloj(clock_1_out),
    .Reset(cu_1_reset_signal_2), .Output(MDR_output));

  // Notes on the sheet:
  //   ROM
  //   contents of rom_1 (hex, n*v repeats v):
  //   701 12*0 800
  //   RAM
endmodule

module CU (
  input  RESET_SIGNAL,
  input  Reloj,
  input  [19:0] IR_INPUT,
  input  [7:0] PC_COUNTER_INPUT,
  input  [12:0] Instruction,
  output RESET_SIGNAL_2,
  output LOAD_SIGNAL,
  output [4:0] LOAD_OP,
  output [4:0] ORIGIN,
  output [3:0] DESTINY,
  output ADVANCE,
  output [3:0] ALU_OPERACION,
  output [7:0] PC_JUMP,
  output [15:0] ROM_STEP,
  output [1:0] PC_OP,
  output RESET_PC
);

  wire and_1_out, comparator_1_eq, demultiplexer_1_out0, demultiplexer_1_out1, demultiplexer_1_out2,
       demultiplexer_1_out3, demultiplexer_1_out4, demultiplexer_1_out5, demultiplexer_1_out6, not_1_out,
       not_2_out;
  wire [7:0] bit_extender_1_out, demultiplexer_2_out0, demultiplexer_2_out1, demultiplexer_2_out2,
       demultiplexer_2_out3, demultiplexer_2_out4, demultiplexer_2_out5, demultiplexer_2_out6;
  wire [7:1] demultiplexer_2_out7;

  BOTON_SIGNAL boton_signal_1 (.RESET_SIGNAL(RESET_SIGNAL), .Reloj(Reloj), .RESET_OUT(RESET_SIGNAL_2));
  CU_Tick_Counter cu_tick_counter_1 (.Reloj(Reloj), .ADVANCE(ADVANCE));
  not not_1 (not_1_out, 1'b0);
  not not_2 (not_2_out, comparator_1_eq);
  Regs_Counter regs_counter_1 (.PC(PC_COUNTER_INPUT));  // open: Load_Index, CONTINUE_LOADING
  Comparator #(.width(12), .mode("unsigned")) comparator_1 (
    .a(Instruction[11:0]), .b(12'h800), .eq(comparator_1_eq));  // open: gt, lt
  and and_1 (and_1_out, not_2_out, ADVANCE, not_1_out);
  CU_STEP cu_step_1 (.ADVANCE_STEP(and_1_out), .RESET(RESET_SIGNAL_2), .Reloj(Reloj), .CURRENT_STATE(ROM_STEP));
  Demultiplexer #(.select(3)) demultiplexer_1 (
    .out0(demultiplexer_1_out0), .out1(demultiplexer_1_out1), .out2(demultiplexer_1_out2),
    .out3(demultiplexer_1_out3), .out4(demultiplexer_1_out4), .out5(demultiplexer_1_out5),
    .out6(demultiplexer_1_out6), .in(1'b1), .sel(Instruction[10:8]));  // open: out7, en
  Demultiplexer #(.select(3), .width(8)) demultiplexer_2 (
    .out0(demultiplexer_2_out0), .out1(demultiplexer_2_out1), .out2(demultiplexer_2_out2),
    .out3(demultiplexer_2_out3), .out4(demultiplexer_2_out4), .out5(demultiplexer_2_out5),
    .out6(demultiplexer_2_out6), .out7({demultiplexer_2_out7, RESET_PC}), .in(bit_extender_1_out),
    .sel(Instruction[10:8]));  // open: en
  assign bit_extender_1_out = {{4{1'b0}}, Instruction[3:0]};  // Bit_Extender bit_extender_1
  Register #(.width(1)) register_1 (
    .D(demultiplexer_2_out0[0]), .en(demultiplexer_1_out0), .Q(LOAD_SIGNAL), .clk(Reloj), .clr(RESET_SIGNAL_2));
  Register #(.width(5)) register_2 (
    .D(demultiplexer_2_out1[4:0]), .en(demultiplexer_1_out1), .Q(LOAD_OP), .clk(Reloj), .clr(RESET_SIGNAL_2));
  Register #(.width(5)) register_3 (
    .D(demultiplexer_2_out2[4:0]), .en(demultiplexer_1_out2), .Q(ORIGIN), .clk(Reloj), .clr(RESET_SIGNAL_2));
  Register #(.width(4)) register_4 (
    .D(demultiplexer_2_out3[3:0]), .en(demultiplexer_1_out3), .Q(DESTINY), .clk(Reloj), .clr(RESET_SIGNAL_2));
  Register #(.width(4)) register_5 (
    .D(demultiplexer_2_out4[3:0]), .en(demultiplexer_1_out4), .Q(ALU_OPERACION), .clk(Reloj),
    .clr(RESET_SIGNAL_2));
  Register register_6 (
    .D(demultiplexer_2_out5), .en(demultiplexer_1_out5), .Q(PC_JUMP), .clk(Reloj), .clr(RESET_SIGNAL_2));
  Register #(.width(2)) register_7 (
    .D(demultiplexer_2_out6[1:0]), .en(demultiplexer_1_out6), .Q(PC_OP), .clk(Reloj), .clr(RESET_SIGNAL_2));
endmodule

module ALU (
  input  [7:0] X,
  input  [7:0] Y,
  input  [3:0] Operacion,
  input  LOAD,
  input  [1:0] LOAD_R_N,
  input  Reloj,
  input  RESET,
  output [7:0] Result
);

  wire demultiplexer_1_out0, demultiplexer_1_out1, demultiplexer_1_out2, demultiplexer_1_out3;
  wire [3:0] register_1_q;
  wire [7:0] and_1_out_3, division_1_out_3, multiplexer_1_out, multiplicacion_1_out_3, nand_1_out_3,
       nor_1_out_3, or_1_out_3, registro_8_bits_1_output, registro_8_bits_2_output, resta_1_out_3,
       suma_1_out_3, xnor_1_out_3, xor_1_out_3;

  Demultiplexer #(.select(2)) demultiplexer_1 (
    .out0(demultiplexer_1_out0), .out1(demultiplexer_1_out1), .out2(demultiplexer_1_out2),
    .out3(demultiplexer_1_out3), .in(LOAD), .sel(LOAD_R_N));  // open: en
  Registro_8_bits registro_8_bits_1 (
    .Load(demultiplexer_1_out0), .Data_In(X), .Reloj(Reloj), .Reset(RESET), .Output(registro_8_bits_1_output));
  Registro_8_bits registro_8_bits_2 (
    .Load(demultiplexer_1_out1), .Data_In(Y), .Reloj(Reloj), .Reset(RESET), .Output(registro_8_bits_2_output));
  SUMA suma_1 (.X(registro_8_bits_1_output), .Y(registro_8_bits_2_output), .out_3(suma_1_out_3));
  RESTA resta_1 (.X(registro_8_bits_1_output), .Y(registro_8_bits_2_output), .out_3(resta_1_out_3));
  MULTIPLICACION multiplicacion_1 (
    .X(registro_8_bits_1_output), .Y(registro_8_bits_2_output), .out_3(multiplicacion_1_out_3));
  DIVISION division_1 (.X(registro_8_bits_1_output), .Y(registro_8_bits_2_output), .out_3(division_1_out_3));
  AND and_1 (.X(registro_8_bits_1_output), .Y(registro_8_bits_2_output), .out_3(and_1_out_3));
  NAND nand_1 (.X(registro_8_bits_1_output), .Y(registro_8_bits_2_output), .out_3(nand_1_out_3));
  OR or_1 (.X(registro_8_bits_1_output), .Y(registro_8_bits_2_output), .out_3(or_1_out_3));
  NOR nor_1 (.X(registro_8_bits_1_output), .Y(registro_8_bits_2_output), .out_3(nor_1_out_3));
  XOR xor_1 (.X(registro_8_bits_1_output), .Y(registro_8_bits_2_output), .out_3(xor_1_out_3));
  XNOR xnor_1 (.X(registro_8_bits_1_output), .Y(registro_8_bits_2_output), .out_3(xnor_1_out_3));
  Register #(.width(4)) register_1 (
    .D(Operacion), .en(demultiplexer_1_out3), .Q(register_1_q), .clk(Reloj), .clr(RESET));
  Multiplexer #(.select(4), .width(8)) multiplexer_1 (
    .in0(suma_1_out_3), .in1(resta_1_out_3), .in2(multiplicacion_1_out_3), .in3(division_1_out_3),
    .in4(and_1_out_3), .in5(nand_1_out_3), .in6(or_1_out_3), .in7(nor_1_out_3), .in8(xor_1_out_3),
    .in9(xnor_1_out_3), .out(multiplexer_1_out), .sel(register_1_q));  // open: in10, in11, in12, in13, in14, in15, en
  Registro_8_bits registro_8_bits_3 (
    .Load(demultiplexer_1_out2), .Data_In(multiplexer_1_out), .Reloj(Reloj), .Reset(RESET), .Output(Result));

  // Notes on the sheet:
  //   0000 - SUMA
  //   0001 - RESTA
  //   0011 - DIVISION
  //   0100 - AND
  //   0101 - NAND
  //   0110 - OR
  //   0111 - NOR
  //   1000 - XOR
  //   1001 - XNOR
  //   Codigos de Operación
  //   0010 - MULTIPLICACION
endmodule

// RAM REGISTER
module Registros_RAM (
  input  [7:0] Input,
  input  Reset,
  input  Reloj,
  input  LOAD,
  output [7:0] O_R0,
  output [7:0] O_R2,
  output [7:0] O_R4,
  output [7:0] O_R6,
  output [7:0] O_R1,
  output [7:0] O_R3,
  output [7:0] O_R5,
  output [7:0] O_R7
);

  Registro_8_bits R0 (.Load(LOAD), .Data_In(Input), .Reloj(Reloj), .Reset(Reset), .Output(O_R0));
  Registro_8_bits R1 (.Load(LOAD), .Data_In(O_R0), .Reloj(Reloj), .Reset(Reset), .Output(O_R1));
  Registro_8_bits R3 (.Load(LOAD), .Data_In(O_R2), .Reloj(Reloj), .Reset(Reset), .Output(O_R3));
  Registro_8_bits R2 (.Load(LOAD), .Data_In(O_R1), .Reloj(Reloj), .Reset(Reset), .Output(O_R2));
  Registro_8_bits R4 (.Load(LOAD), .Data_In(O_R3), .Reloj(Reloj), .Reset(Reset), .Output(O_R4));
  Registro_8_bits R5 (.Load(LOAD), .Data_In(O_R4), .Reloj(Reloj), .Reset(Reset), .Output(O_R5));
  Registro_8_bits R7 (.Load(LOAD), .Data_In(O_R6), .Reloj(Reloj), .Reset(Reset), .Output(O_R7));
  Registro_8_bits R6 (.Load(LOAD), .Data_In(O_R5), .Reloj(Reloj), .Reset(Reset), .Output(O_R6));

  // Notes on the sheet:
  //   000 Registro 0
  //   001 Registro 1
  //   010 Registro 2
  //   011 Registro 3
  //   100 Registro 4
  //   101 Registro 5
  //   110 Registro 6
  //   111 Registro 7
endmodule

// GEN. REGISTER
module Registros_Generales (
  input  RESET,
  input  Reloj,
  input  [7:0] In_R1,
  input  [7:0] In_R3,
  input  [7:0] In_R5,
  input  [7:0] In_R7,
  input  [7:0] In_R0,
  input  [7:0] In_R2,
  input  [7:0] In_R4,
  input  [7:0] In_R6,
  input  [2:0] LOAD_R_N,
  input  LOAD,
  output [7:0] O_R0,
  output [7:0] O_R2,
  output [7:0] O_R4,
  output [7:0] O_R6,
  output [7:0] O_R1,
  output [7:0] O_R3,
  output [7:0] O_R5,
  output [7:0] O_R7
);

  wire demultiplexer_1_out0, demultiplexer_1_out1, demultiplexer_1_out2, demultiplexer_1_out3,
       demultiplexer_1_out4, demultiplexer_1_out5, demultiplexer_1_out6, demultiplexer_1_out7;

  Registro_8_bits R0 (.Load(demultiplexer_1_out0), .Data_In(In_R0), .Reloj(Reloj), .Reset(RESET), .Output(O_R0));
  Registro_8_bits R1 (.Load(demultiplexer_1_out1), .Data_In(In_R1), .Reloj(Reloj), .Reset(RESET), .Output(O_R1));
  Demultiplexer #(.select(3)) demultiplexer_1 (
    .out0(demultiplexer_1_out0), .out1(demultiplexer_1_out1), .out2(demultiplexer_1_out2),
    .out3(demultiplexer_1_out3), .out4(demultiplexer_1_out4), .out5(demultiplexer_1_out5),
    .out6(demultiplexer_1_out6), .out7(demultiplexer_1_out7), .in(LOAD), .sel(LOAD_R_N));  // open: en
  Registro_8_bits R2 (.Load(demultiplexer_1_out2), .Data_In(In_R2), .Reloj(Reloj), .Reset(RESET), .Output(O_R2));
  Registro_8_bits R3 (.Load(demultiplexer_1_out3), .Data_In(In_R3), .Reloj(Reloj), .Reset(RESET), .Output(O_R3));
  Registro_8_bits R4 (.Load(demultiplexer_1_out4), .Data_In(In_R4), .Reloj(Reloj), .Reset(RESET), .Output(O_R4));
  Registro_8_bits R5 (.Load(demultiplexer_1_out5), .Data_In(In_R5), .Reloj(Reloj), .Reset(RESET), .Output(O_R5));
  Registro_8_bits R6 (.Load(demultiplexer_1_out6), .Data_In(In_R6), .Reloj(Reloj), .Reset(RESET), .Output(O_R6));
  Registro_8_bits R7 (.Load(demultiplexer_1_out7), .Data_In(In_R7), .Reloj(Reloj), .Reset(RESET), .Output(O_R7));

  // Notes on the sheet:
  //   000 Registro 0
  //   001 Registro 1
  //   010 Registro 2
  //   011 Registro 3
  //   100 Registro 4
  //   101 Registro 5
  //   110 Registro 6
  //   111 Registro 7
endmodule

module PC (
  input  Reloj,
  input  [7:0] Dato_Salto,
  input  RESET,
  input  [1:0] PC_INSTRUCTION,
  output [7:0] Dato_Salida
);

  wire demultiplexer_1_out1, demultiplexer_1_out2;
  wire [7:0] adder_1_out, bit_extender_1_out, multiplexer_1_out;

  Register register_1 (.D(multiplexer_1_out), .en(1'b1), .Q(Dato_Salida), .clk(Reloj), .clr(RESET));
  assign bit_extender_1_out = {{7{1'b0}}, demultiplexer_1_out1};  // Bit_Extender bit_extender_1
  Demultiplexer #(.select(2)) demultiplexer_1 (
    .out1(demultiplexer_1_out1), .out2(demultiplexer_1_out2), .in(1'b1), .sel(PC_INSTRUCTION));  // open: out0, out3, en
  Adder adder_1 (.a(Dato_Salida), .b(bit_extender_1_out), .out(adder_1_out));  // open: cin, cout
  Multiplexer #(.width(8)) multiplexer_1 (
    .in0(adder_1_out), .in1(Dato_Salto), .out(multiplexer_1_out), .sel(demultiplexer_1_out2));  // open: en

  // Notes on the sheet:
  //   00 Mantener PC
  //   01 INC PC
  //   10 LOAD PC
endmodule

module Registro_8_bits (
  input  Load,
  input  [7:0] Data_In,
  input  Reloj,
  input  Reset,
  output [7:0] Output
);

  Register register_1 (.D(Data_In), .en(Load), .Q(Output), .clk(Reloj), .clr(Reset));
endmodule

// LOADER
module Loader_Manager (
  input  LOAD_SIGNAL,
  input  [4:0] LOAD_OP,
  output LOAD_RAM_Register,
  output [2:0] General_Register_OP,
  output LOAD_General_Register,
  output [1:0] ALU_Register_N,
  output LOAD_ALU,
  output LOAD_MDR,
  output LOAD_IN_RAM,
  output [1:0] IR_OP,
  output LOAD_IR
);

  wire demultiplexer_1_out1, demultiplexer_1_out2, demultiplexer_1_out3, demultiplexer_1_out4,
       demultiplexer_1_out5, demultiplexer_1_out6, demultiplexer_1_out7, demultiplexer_1_out8,
       demultiplexer_1_out9, demultiplexer_1_out10, demultiplexer_1_out11, demultiplexer_1_out12,
       demultiplexer_1_out15, demultiplexer_1_out16, demultiplexer_1_out17;

  Demultiplexer #(.select(5)) demultiplexer_1 (
    .out0(LOAD_RAM_Register), .out1(demultiplexer_1_out1), .out2(demultiplexer_1_out2),
    .out3(demultiplexer_1_out3), .out4(demultiplexer_1_out4), .out5(demultiplexer_1_out5),
    .out6(demultiplexer_1_out6), .out7(demultiplexer_1_out7), .out8(demultiplexer_1_out8),
    .out9(demultiplexer_1_out9), .out10(demultiplexer_1_out10), .out11(demultiplexer_1_out11),
    .out12(demultiplexer_1_out12), .out13(LOAD_MDR), .out14(LOAD_IN_RAM), .out15(demultiplexer_1_out15),
    .out16(demultiplexer_1_out16), .out17(demultiplexer_1_out17), .in(LOAD_SIGNAL), .sel(LOAD_OP));  // open: out18, out19, out20, out21, out22, out23, out24, out25, out26, out27, out28, out29, out30, out31, en
  Priority_Encoder priority_encoder_1 (
    .in0(demultiplexer_1_out1), .in1(demultiplexer_1_out2), .in2(demultiplexer_1_out3),
    .in3(demultiplexer_1_out4), .in4(demultiplexer_1_out5), .in5(demultiplexer_1_out6),
    .in6(demultiplexer_1_out7), .in7(demultiplexer_1_out8), .out(General_Register_OP),
    .gs(LOAD_General_Register));  // open: en_in, en_out
  Priority_Encoder #(.select(2)) priority_encoder_2 (
    .in0(demultiplexer_1_out9), .in1(demultiplexer_1_out10), .in2(demultiplexer_1_out11),
    .in3(demultiplexer_1_out12), .out(ALU_Register_N), .gs(LOAD_ALU));  // open: en_out, en_in
  Priority_Encoder #(.select(2)) priority_encoder_3 (
    .in0(demultiplexer_1_out15), .in1(demultiplexer_1_out16), .in2(demultiplexer_1_out17), .out(IR_OP),
    .gs(LOAD_IR));  // open: in3, en_out, en_in
endmodule

// IR
module Instruction_Register (
  input  Reset,
  input  [7:0] Dato_In_R0,
  input  [3:0] Dato_OPCODE,
  input  Load,
  input  [1:0] LOAD_R_N,
  input  [7:0] Dato_In_R1,
  input  Reloj,
  output [19:0] Output
);

  wire demultiplexer_1_out0, demultiplexer_1_out1, demultiplexer_1_out2;

  Demultiplexer #(.select(2)) demultiplexer_1 (
    .out0(demultiplexer_1_out0), .out1(demultiplexer_1_out1), .out2(demultiplexer_1_out2), .in(Load),
    .sel(LOAD_R_N));  // open: out3, en
  Register register_1 (.D(Dato_In_R0), .en(demultiplexer_1_out0), .Q(Output[7:0]), .clk(Reloj), .clr(Reset));
  Register #(.width(4)) register_2 (.D(Dato_OPCODE), .en(demultiplexer_1_out1), .Q(Output[19:16]));  // open: clk, clr
  Register register_3 (.D(Dato_In_R1), .en(demultiplexer_1_out2), .Q(Output[15:8]), .clk(Reloj), .clr(Reset));
endmodule

// ROUTER MANAGER
module Router_Manager (
  input  [7:0] In_R0_RAM,
  input  [7:0] In_R1_RAM,
  input  [7:0] In_R2_RAM,
  input  [7:0] In_R3_RAM,
  input  [7:0] In_R4_RAM,
  input  [7:0] In_R5_RAM,
  input  [7:0] In_R6_RAM,
  input  [7:0] In_R7_RAM,
  input  [7:0] In_R0_General,
  input  [7:0] In_R1_General,
  input  [7:0] In_R2_General,
  input  [7:0] In_R3_General,
  input  [7:0] In_R4_General,
  input  [7:0] In_R5_General,
  input  [7:0] In_R6_General,
  input  [7:0] In_R7_General,
  input  [7:0] IN_ALU_R,
  input  [3:0] DESTINY,
  input  [4:0] ORIGIN,
  output [7:0] OUT_R0_General,
  output [7:0] OUT_R1_General,
  output [7:0] OUT_R2_General,
  output [7:0] OUT_R3_General,
  output [7:0] OUT_R4_General,
  output [7:0] OUT_R5_General,
  output [7:0] OUT_R6_General,
  output [7:0] OUT_R7_General,
  output [7:0] OUT_MDR,
  output [7:0] OUT_ALU_X,
  output [7:0] OUT_ALU_Y,
  output [3:0] OUT_IR_OPCODE,
  output [7:0] OUT_IR_R0,
  output [7:0] OUT_IR_R0_2
);

  wire [7:0] multiplexer_1_out;
  wire [7:4] demultiplexer_1_out11;

  Multiplexer #(.select(5), .width(8)) multiplexer_1 (
    .in0(In_R0_RAM), .in1(In_R1_RAM), .in2(In_R2_RAM), .in3(In_R3_RAM), .in4(In_R4_RAM), .in5(In_R5_RAM),
    .in6(In_R6_RAM), .in7(In_R7_RAM), .in8(In_R0_General), .in9(In_R1_General), .in10(In_R2_General),
    .in11(In_R3_General), .in12(In_R4_General), .in13(In_R5_General), .in14(In_R6_General),
    .in15(In_R7_General), .in16(IN_ALU_R), .out(multiplexer_1_out), .sel(ORIGIN));  // open: in17, in18, in19, in20, in21, in22, in23, in24, in25, in26, in27, in28, in29, in30, in31, en
  Demultiplexer #(.select(4), .width(8)) demultiplexer_1 (
    .out0(OUT_R0_General), .out1(OUT_R1_General), .out2(OUT_R2_General), .out3(OUT_R3_General),
    .out4(OUT_R4_General), .out5(OUT_R5_General), .out6(OUT_R6_General), .out7(OUT_R7_General),
    .out8(OUT_MDR), .out9(OUT_ALU_X), .out10(OUT_ALU_Y), .out11({demultiplexer_1_out11, OUT_IR_OPCODE}),
    .out12(OUT_IR_R0), .out13(OUT_IR_R0_2), .in(multiplexer_1_out), .sel(DESTINY));  // open: out14, out15, en
endmodule

module SUMA (
  input  [7:0] X,
  input  [7:0] Y,
  output [7:0] out_3
);

  Adder adder_1 (.a(X), .b(Y), .out(out_3));  // open: cin, cout
  RAM ram_1 ();  // open: addr, data, sel, clk, ld, clr
endmodule

module RESTA (
  input  [7:0] X,
  input  [7:0] Y,
  output [7:0] out_3
);

  Subtractor subtractor_1 (.a(X), .b(Y), .out(out_3));  // open: bin, bout
endmodule

module MULTIPLICACION (
  input  [7:0] X,
  input  [7:0] Y,
  output [7:0] out_3
);

  Multiplier multiplier_1 (.a(X), .b(Y), .out(out_3));  // open: cin, cout
endmodule

module DIVISION (
  input  [7:0] X,
  input  [7:0] Y,
  output [7:0] out_3
);

  Divider divider_1 (.a(X), .b(Y), .out(out_3));  // open: upper, rem
endmodule

module AND (
  input  [7:0] X,
  input  [7:0] Y,
  output [7:0] out_3
);

  and and_1 (out_3[0], X[0], Y[0]);
  and and_2 (out_3[1], X[1], Y[1]);
  and and_3 (out_3[2], X[2], Y[2]);
  and and_4 (out_3[3], X[3], Y[3]);
  and and_5 (out_3[4], X[4], Y[4]);
  and and_6 (out_3[5], X[5], Y[5]);
  and and_7 (out_3[6], X[6], Y[6]);
  and and_8 (out_3[7], X[7], Y[7]);
endmodule

module NAND (
  input  [7:0] X,
  input  [7:0] Y,
  output [7:0] out_3
);

  nand nand_1 (out_3[0], X[0], Y[0]);
  nand nand_2 (out_3[1], X[1], Y[1]);
  nand nand_3 (out_3[2], X[2], Y[2]);
  nand nand_4 (out_3[3], X[3], Y[3]);
  nand nand_5 (out_3[4], X[4], Y[4]);
  nand nand_6 (out_3[5], X[5], Y[5]);
  nand nand_7 (out_3[6], X[6], Y[6]);
  nand nand_8 (out_3[7], X[7], Y[7]);
endmodule

module OR (
  input  [7:0] X,
  input  [7:0] Y,
  output [7:0] out_3
);

  or or_1 (out_3[0], X[0], Y[0]);
  or or_2 (out_3[1], X[1], Y[1]);
  or or_3 (out_3[2], X[2], Y[2]);
  or or_4 (out_3[3], X[3], Y[3]);
  or or_5 (out_3[4], X[4], Y[4]);
  or or_6 (out_3[5], X[5], Y[5]);
  or or_7 (out_3[6], X[6], Y[6]);
  or or_8 (out_3[7], X[7], Y[7]);
endmodule

module NOR (
  input  [7:0] X,
  input  [7:0] Y,
  output [7:0] out_3
);

  nor nor_1 (out_3[0], X[0], Y[0]);
  nor nor_2 (out_3[1], X[1], Y[1]);
  nor nor_3 (out_3[2], X[2], Y[2]);
  nor nor_4 (out_3[3], X[3], Y[3]);
  nor nor_5 (out_3[4], X[4], Y[4]);
  nor nor_6 (out_3[5], X[5], Y[5]);
  nor nor_7 (out_3[6], X[6], Y[6]);
  nor nor_8 (out_3[7], X[7], Y[7]);
endmodule

module XOR (
  input  [7:0] X,
  input  [7:0] Y,
  output [7:0] out_3
);

  xor xor_1 (out_3[0], X[0], Y[0]);
  xor xor_2 (out_3[1], X[1], Y[1]);
  xor xor_3 (out_3[2], X[2], Y[2]);
  xor xor_4 (out_3[3], X[3], Y[3]);
  xor xor_5 (out_3[4], X[4], Y[4]);
  xor xor_6 (out_3[5], X[5], Y[5]);
  xor xor_7 (out_3[6], X[6], Y[6]);
  xor xor_8 (out_3[7], X[7], Y[7]);
endmodule

module XNOR (
  input  [7:0] X,
  input  [7:0] Y,
  output [7:0] out_3
);

  xnor xnor_1 (out_3[0], X[0], Y[0]);
  xnor xnor_2 (out_3[1], X[1], Y[1]);
  xnor xnor_3 (out_3[2], X[2], Y[2]);
  xnor xnor_4 (out_3[3], X[3], Y[3]);
  xnor xnor_5 (out_3[4], X[4], Y[4]);
  xnor xnor_6 (out_3[5], X[5], Y[5]);
  xnor xnor_7 (out_3[6], X[6], Y[6]);
  xnor xnor_8 (out_3[7], X[7], Y[7]);
endmodule

// BTN
module BOTON_SIGNAL (
  input  RESET_SIGNAL,
  input  Reloj,
  output RESET_OUT
);

  wire d_ff_1_q, not_1_out;

  D_Flip_Flop d_ff_1 (.clk(Reloj), .D(RESET_SIGNAL), .Q(d_ff_1_q));  // open: Qn, preset, en, reset
  not not_1 (not_1_out, d_ff_1_q);
  and and_1 (RESET_OUT, RESET_SIGNAL, not_1_out);
endmodule

module CU_Tick_Counter (
  input  Reloj,
  output ADVANCE
);

  wire not_1_out, Tick_Reg_q;

  Register #(.width(1)) Tick_Reg (.D(not_1_out), .en(1'b1), .Q(Tick_Reg_q), .clk(Reloj), .clr(1'b0));
  not not_1 (not_1_out, Tick_Reg_q);
  Comparator #(.width(1)) comparator_1 (.a(Tick_Reg_q), .b(1'b1), .eq(ADVANCE));  // open: gt, lt
endmodule

module Regs_Counter (
  input  [7:0] PC,
  input  [7:0] Load_Index,
  output CONTINUE_LOADING
);

  wire comparator_1_eq, comparator_2_eq, comparator_3_lt, or_1_out;
  wire [7:0] multiplexer_1_out;

  Comparator #(.width(5), .mode("unsigned")) comparator_1 (
    .a(Load_Index[4:0]), .b(5'b00011), .eq(comparator_1_eq));  // open: gt, lt
  Comparator #(.width(5), .mode("unsigned")) comparator_2 (
    .a(Load_Index[4:0]), .b(5'b01001), .eq(comparator_2_eq));  // open: gt, lt
  Multiplexer #(.width(8)) multiplexer_1 (
    .in0({8{1'b1}}), .in1(8'h7), .out(multiplexer_1_out), .sel(comparator_2_eq));  // open: en
  Comparator #(.mode("unsigned")) comparator_3 (.a(PC), .b(multiplexer_1_out), .lt(comparator_3_lt));  // open: gt, eq
  or or_1 (or_1_out, comparator_1_eq, comparator_2_eq);
  and and_1 (CONTINUE_LOADING, comparator_3_lt, or_1_out);
endmodule

// STEP
module CU_STEP (
  input  RESET,
  input  ADVANCE_STEP,
  input  Reloj,
  output [15:0] CURRENT_STATE
);

  wire [15:0] adder_1_out;

  Adder #(.width(16)) adder_1 (.a(CURRENT_STATE), .b(16'h1), .out(adder_1_out));  // open: cin, cout
  Register #(.width(16)) register_1 (.D(adder_1_out), .en(ADVANCE_STEP), .Q(CURRENT_STATE), .clk(Reloj), .clr(RESET));
endmodule
